# Fritzing sketch A0Circuit (saved by Fritzing 0.9.3b)
breadboards: 1

parts:
  Part1 = Arduino Due (Rev2b)
  R1 = Resistor [tolerance=±5% resistance=10 package=THT]
  S1 = Pushbutton [package="[THT]"]
  LED1 = LED - 5mm [color="Red (633nm)" package="5 mm [THT]"]
  LED3 = LED - 5mm [color="Red (633nm)" package="5 mm [THT]"]
  LED4 = LED - 5mm [color="Green (565nm)" package="5 mm [THT]"]
  LED5 = LED - 5mm [color="Green (565nm)" package="5 mm [THT]"]
  LED6 = LED - 5mm [color="Red (633nm)" package="5 mm [THT]"]
  LED7 = LED - 5mm [color="Red (633nm)" package="5 mm [THT]"]
  LED8 = LED - 5mm [color="Red (633nm)" package="5 mm [THT]"]
  R2 = Resistor [tolerance=±5% resistance=10 package=THT]
  R3 = Resistor [tolerance=±5% resistance=10 package=THT]
  R4 = Resistor [tolerance=±5% resistance=10 package=THT]
  R5 = Resistor [tolerance=±5% resistance=10 package=THT]
  R6 = Resistor [tolerance=±5% resistance=10 package=THT]
  R7 = Resistor [tolerance=±5% resistance=10 package=THT]
  R8 = Resistor [tolerance=±5% resistance=10 package=THT]
  LED2 = LED - 5mm [color="Red (633nm)" package="5 mm [THT]"]

nets:
  N1: Part1.D8_PWM, LED2.anode
  N2: Part1.D9_PWM, LED1.anode
  N3: Part1.D10_PWM/SS0, S1.Pin_1, S1.Pin_2
  N4: Part1.GND, S1.Pin_3, S1.Pin_4
  N5: Part1.D2_PWM, LED8.anode
  N6: Part1.D3_PWM, LED7.anode
  N7: Part1.D4_PWM/SS1, LED6.anode
  N8: Part1.D5_PWM, LED5.anode
  N9: Part1.D6_PWM, LED4.anode
  N10: Part1.D7_PWM, LED3.anode
  N11: R1.Pin_1, LED1.cathode
  N12: LED3.cathode, R3.Pin_1
  N13: LED4.cathode, R4.Pin_1
  N14: LED5.cathode, R5.Pin_1
  N15: LED6.cathode, R6.Pin_1
  N16: LED7.cathode, R7.Pin_1
  N17: LED8.cathode, R8.Pin_1
  N18: R2.Pin_1, LED2.cathode
